# Fritzing sketch garage_door (saved by Fritzing 0.9.3b)
stripboards: 3

parts:
  M3 = DOIT Esp32 DevKit v1 (30 pins long, 11 pins width) [part_number=ESP32S-PIN30]
  U19 = 4N25 [package=THT]
  U20 = 4N25 [package=THT]
  U21 = 4N25 [package=THT]
  J56 = male pin header, 4 pins [form="♂ (male)"]
  J57 = male pin header, 4 pins [form="♂ (male)"]
  R47 = Resistor [tolerance=±5% resistance=47 package=THT]
  R48 = Resistor [tolerance=±5% resistance=47 package=THT]
  R49 = Resistor [tolerance=±5% resistance=10k package=THT]
  R50 = Resistor [tolerance=±5% resistance=10k package=THT]
  R51 = Resistor [tolerance=±5% resistance=220 package=THT]
  J60 = female pin header, 15 pins [form="♀ (female)"]
  J55 = male pin header, 1 pin [form="♂ (male)"]
  J58 = female pin header, 2 pins [form="♀ (female)"]  # not connected
  J59 = female pin header, 4 pins [form="♀ (female)"]
  U22 = 4N25 [package=THT]
  U23 = 4N25 [package=THT]
  U24 = 4N25 [package=THT]
  J61 = male pin header, 1 pin [form="♂ (male)"]
  J62 = male pin header, 4 pins [form="♂ (male)"]
  J63 = male pin header, 4 pins [form="♂ (male)"]
  R52 = Resistor [tolerance=±5% resistance=47 package=THT]
  R53 = Resistor [tolerance=±5% resistance=47 package=THT]
  R54 = Resistor [tolerance=±5% resistance=10k package=THT]  # not connected
  R55 = Resistor [tolerance=±5% resistance=10k package=THT]  # not connected
  R56 = Resistor [tolerance=±5% resistance=220 package=THT]
  J64 = female pin header, 2 pins [form="♀ (female)"]  # not connected
  J65 = female pin header, 4 pins [form="♀ (female)"]
  J66 = female pin header, 15 pins [form="♀ (female)"]

nets:
  N1: M3.GND, U19.Pin_4, U20.Pin_4, R51.Pin_0, J60.pin2
  N2: M3.RX2, U21.Pin_1, J60.pin6
  N3: M3.D18, R50.Pin_1, J60.pin9
  N4: M3.D19, R49.Pin_0, J60.pin10
  N5: U19.Pin_1, J57.pin2
  N6: U19.Pin_2, R47.Pin_0
  N7: U19.Pin_5, R50.Pin_0
  N8: U20.Pin_1, J57.pin3
  N9: U20.Pin_2, R48.Pin_0
  N10: U20.Pin_5, R49.Pin_1
  N11: U21.Pin_2, R51.Pin_1
  N12: U21.Pin_4, J56.pin1, J57.pin1
  N13: U21.Pin_5, J55.pin1
  N14: J56.pin2, R47.Pin_1
  N15: J56.pin3, R48.Pin_1
  N16: J56.pin4, J57.pin4
  N17: J59.pin1, J59.pin2, J59.pin3
  N18: U22.Pin_1, J63.pin2
  N19: U22.Pin_2, R52.Pin_0
  N20: U22.Pin_4, U23.Pin_4, R56.Pin_0, J66.pin2
  N21: U22.Pin_5, J66.pin9
  N22: U23.Pin_1, J63.pin3
  N23: U23.Pin_2, R53.Pin_0
  N24: U23.Pin_5, J66.pin10
  N25: U24.Pin_1, J66.pin6
  N26: U24.Pin_2, R56.Pin_1
  N27: U24.Pin_4, J62.pin1, J63.pin1
  N28: U24.Pin_5, J61.pin1
  N29: J62.pin2, R52.Pin_1
  N30: J62.pin3, R53.Pin_1
  N31: J62.pin4, J63.pin4
  N32: J65.pin1, J65.pin2, J65.pin3

custom parts:
  DOIT Esp32 DevKit v1 (30 pins long, 11 pins width): The DOIT Esp32 DevKit v1 is one of the development board created by DOIT to evaluate the ESP-WROOM-32 module. It is based on the ESP32 microcontroller that boasts Wifi, Bluetooth, Ethernet and Low Power support all in a single chip. (vanepp) made breadboard work, adjusted pin numbering and labels and reduced size of schematic and cleaned up pcb. This chip is 30pins long (2 x15) and 11 pins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
  4N25: Optocoupler
